# Fritzing sketch pyta (saved by Fritzing 0.9.3b)
breadboards: 1

parts:
  MCU = Arduino Pro Mini v13
  P1 = TRIMPOT [package=trimpot_pth_s3_lock]
  R3 = Resistor [tolerance=±5% resistance=220 package="0603 [SMD]"]
  Q1 = TRANSISTOR_NPN [package=to-92]
  R4 = Resistor [tolerance=±5% resistance=2.5k package="1206 [SMD]"]
  Q2 = Basic FET P-Channel [package="DPak [SMD]"]
  R5 = Resistor [tolerance=±5% resistance=2.5k package="1206 [SMD]"]
  R6 = Resistor [tolerance=±5% resistance=220 package="0603 [SMD]"]
  LED3 = LED - 5mm [color="Red (633nm)" package="5 mm [THT]"]
  VCC1 = Battery block 9V
  D1 = P1000K [part_number=P1000K]
  L1 = Solenoid
  D2 = P1000K [part_number=P1000K]
  S1 = SPST Switch [package=r_sw_th]
  S2 = Momentary Switch [package=ksa_sealed_tac_switch]
  S3 = Momentary Switch [package=ksa_sealed_tac_switch]
  S5 = Momentary Switch [package=ksa_sealed_tac_switch]
  STEP_UP = V_REG_MIC2920 [package=sot223]
  U1 = LCD-16X2 [package=lcd-16x2]
  S4 = Momentary Switch [package=ksa_sealed_tac_switch]
  LED4 = LED - 5mm [color="Red (633nm)" package="5 mm [THT]"]

nets:
  N1: MCU.D1/RX, R5.Pin_1, R6.Pin_1
  VCC: MCU.VCC, P1.CCW, STEP_UP.IN, U1.VDD, U1.A
  GND: MCU.GND, P1.CW, Q1.E, VCC1.-, S2.3, S3.3, S5.3, U1.VSS, S4.3, LED4.cathode
  N2: MCU.RAW, S1.S
  N3: MCU.D13/SCK, U1.DB7
  N4: MCU.D12/MISO, U1.DB6
  N5: MCU.D11_PWM/MOSI, U1.DB5
  N6: MCU.D10_PWM/SS, U1.DB4
  N7: MCU.D9_PWM, U1.E
  N8: MCU.D8, U1.RS
  N9: MCU.D7, R4.Pin_0
  N10: MCU.D6_PWM, R3.Pin_0
  N11: MCU.D5_PWM, S5.1
  N12: MCU.D4, S4.1
  N13: MCU.D3_PWM, S3.1
  N14: MCU.D2, S2.1
  N15: P1.WIPER, U1.VO
  N16: R3.Pin_1, LED4.anode
  N17: Q1.B, R4.Pin_1
  N18: Q1.C, U1.K
  N19: Q2.Gate, R5.Pin_0, LED3.cathode
  N20: Q2.drain, STEP_UP.OUT
  N21: Q2.source, D1.cathode, L1.pin1
  N22: R6.Pin_0, LED3.anode
  N23: VCC1.+, D2.anode
  N24: D1.anode, L1.pin2, STEP_UP.GND
  N25: D2.cathode, S1.P
